# Fritzing sketch Wiring (saved by Fritzing 0.9.3b)
breadboards: 1
stripboards: 1

parts:
  Part2 = Arduino Uno (Rev3)
  Part3 = Bluetooth HC-05 Macho  # not connected
  S2 = Pushbutton [package="[THT]"]
  S3 = Pushbutton [package="[THT]"]
  S4 = Pushbutton [package="[THT]"]
  S5 = Pushbutton [package="[THT]"]
  S6 = Pushbutton [package="[THT]"]
  S1 = Pushbutton [package="[THT]"]
  R1 = Resistor [tolerance=±5% resistance=220 package=THT]
  R2 = Resistor [tolerance=±5% resistance=220 package=THT]
  R3 = Resistor [tolerance=±5% resistance=220 package=THT]
  R4 = Resistor [tolerance=±5% resistance=220 package=THT]
  R5 = Resistor [tolerance=±5% resistance=220 package=THT]
  R6 = Resistor [tolerance=±5% resistance=220 package=THT]
  R7 = Resistor [tolerance=±5% resistance=10k package=THT]
  R8 = Resistor [tolerance=±5% resistance=10k package=THT]
  R9 = Resistor [tolerance=±5% resistance=10k package=THT]
  R10 = Resistor [tolerance=±5% resistance=10k package=THT]
  R11 = Resistor [tolerance=±5% resistance=10k package=THT]
  R12 = Resistor [tolerance=±5% resistance=10k package=THT]

nets:
  N1: Part2.D8, R1.Pin_1
  N2: Part2.D9_PWM, R2.Pin_1
  N3: Part2.D10_PWM/SS, R3.Pin_1
  N4: Part2.D11_PWM/MOSI, R4.Pin_1
  N5: Part2.D12/MISO, R5.Pin_1
  N6: Part2.D13/SCK, R6.Pin_1
  N7: Part2.5V, R7.Pin_0, R8.Pin_0, R9.Pin_0, R10.Pin_0, R11.Pin_0, R12.Pin_0
  N8: Part2.GND, S2.Pin_3, S2.Pin_4, S3.Pin_3, S3.Pin_4, S4.Pin_3, S4.Pin_4, S5.Pin_3, S5.Pin_4, S6.Pin_3, S6.Pin_4, S1.Pin_3, S1.Pin_4
  N9: S2.Pin_1, S2.Pin_2, R2.Pin_0, R8.Pin_1
  N10: S3.Pin_1, S3.Pin_2, R3.Pin_0, R9.Pin_1
  N11: S4.Pin_1, S4.Pin_2, R4.Pin_0, R10.Pin_1
  N12: S5.Pin_1, S5.Pin_2, R5.Pin_0, R11.Pin_1
  N13: S6.Pin_1, S6.Pin_2, R6.Pin_0, R12.Pin_1
  N14: S1.Pin_1, S1.Pin_2, R1.Pin_0, R7.Pin_1
